# Fritzing sketch diagram (saved by Fritzing 0.9.3b)

parts:
  ARDUINO = Arduino Uno (Rev3)
  Mod1 = KY-019 5V Relay Module [package="Breakout board"]
  S1 = Toggle Switch [package=THT]
  LED3 = LED - 5mm [color="Green (555nm)" package="5 mm [THT]"]
  LED4 = LED - 5mm [color="Red (633nm)" package="5 mm [THT]"]

nets:
  N1: ARDUINO.D9_PWM, LED4.anode
  N2: ARDUINO.D10_PWM/SS, LED3.anode
  N3: ARDUINO.D5_PWM, Mod1.S
  N4: ARDUINO.D7, S1.COM
  N5: ARDUINO.5V, Mod1.+, S1.L1
  N6: ARDUINO.GND, Mod1.-, S1.L2, LED3.cathode, LED4.cathode

custom parts:
  KY-019 5V Relay Module: KY-019 5V Relay module, used to control AC circuits. (Special thanks to vanepp for fixing the PCB holes and other errors)
